# Fritzing sketch Circuito PCM PCB (saved by Fritzing 0.9.3b)
perfboards: 1

parts:
  LCM1602_IIC3 = LCM1602 IIC [part_number="LCM1602 IIC" chip_label="LCM1602 IIC" package="DIP (Dual Inline) [THT]"]
  LCD4 = LCD screen  # not connected
  Componente4 = Arduino Nano (Rev3.0)
  microSD3 = MicroSD Card Module
  S8 = Momentary Switch [package=ksa_sealed_tac_switch]
  S9 = Momentary Switch [package=ksa_sealed_tac_switch]
  S10 = Momentary Switch [package=ksa_sealed_tac_switch]
  R12 = Resistor [tolerance=±5% power=0.25 resistance=10k package=THT]
  R13 = Resistor [tolerance=±5% power=0.25 resistance=10k package=THT]
  R14 = Resistor [tolerance=±5% power=0.25 resistance=10k package=THT]

nets:
  N1: LCM1602_IIC3.SDA, Componente4.A4
  N2: LCM1602_IIC3.SCL, Componente4.A5
  N3: LCM1602_IIC3.LED_A, LCM1602_IIC3.LED_B
  N4: Componente4.GND, R14.Pin_1
  N5: Componente4.D3, S10.3
  N6: Componente4.D4, S9.3
  N7: Componente4.D5, S8.3
  N8: Componente4.D10, microSD3.CS
  N9: Componente4.D11/MOSI, microSD3.MOSI
  N10: Componente4.D12/MISO, microSD3.MISO
  N11: Componente4.5V, S8.2
  N12: Componente4.D13/SCK, microSD3.SCK
  N13: S8.4, R13.Pin_0
  N14: S9.4, R12.Pin_0
  N15: S10.4, R14.Pin_0

custom parts:
  LCM1602 IIC: I2C-Module to use a 1602 or 2004 LCD on with the wire.h libory Serial LCD Modul
